// Logisim project jrmips.circ as structural Verilog: 6 circuits, main circuit main
module main (
  output [15:0] rs,
  output [15:0] rt_or_Imm
);

  wire BN_p4, BP_p1, branch_control_1_bn, branch_control_1_bp, branch_control_1_bx, branch_control_1_bz,
       BX_p1, BZ_p4, Clear_PC__Registers__and_Put_out, Clear_RAM_out, CLOCK_out, control_1_addi,
       control_1_alusrc, control_1_branch, control_1_memread, control_1_memtoreg, control_1_memwrite,
       control_1_put, control_1_regwrite, control_1_shift, not_1_p1, not_1_p2, not_2_p2, not_3_p1, not_3_p2,
       not_4_p2, or_1_p2, or_2_p2, or_3_p5;
  wire [1:0] control_1_aluop0;
  wire [2:0] jump_control_1_output;
  wire [3:0] multiplexer_3_out, register_1_q_2, register_1_q_3;
  wire [7:0] adder_1_out, multiplexer_2_out, multiplexer_4_out, multiplexer_9_out, PC_q, register_1_q;
  wire [15:0] bit_extender_1_out, bit_extender_2_out, bit_extender_3_out, multiplexer_1_out,
       multiplexer_5_out, multiplexer_7_out, multiplexer_8_out, multiplexer_10_out, multiplexer_11_out,
       n16_bit_alu_1_result, ram_1_data, registers_1_read_data_2, rom_1_data, shifter_1_out, shifter_2_out;

  // NOT_Gate not_1: pin names not known; wires that end beside it: not_1_p1, not_1_p2
  Register PC (.D(multiplexer_2_out), .en(not_1_p2), .Q(PC_q), .clk(CLOCK_out), .clr(Clear_PC__Registers__and_Put_out));
  Clock CLOCK (.out(CLOCK_out));
  Button Clear_PC__Registers__and_Put (.out(Clear_PC__Registers__and_Put_out));
  LED Halted (.in(not_1_p1));
  Button Clear_RAM (.out(Clear_RAM_out));
  Hex_Digit_Display hex_digit_display_1 (.value(register_1_q_3));  // open: dp
  Adder adder_1 (.a(8'h1), .b(PC_q), .out(adder_1_out));  // open: cin, cout
  Hex_Digit_Display hex_digit_display_2 (.value(register_1_q_2));  // open: dp
  Hex_Digit_Display hex_digit_display_3 (.value(register_1_q[7:4]));  // open: dp
  Register #(.width(16)) register_1 (
    .D(rs), .en(control_1_put), .Q({register_1_q_3, register_1_q_2, register_1_q}), .clk(CLOCK_out),
    .clr(Clear_PC__Registers__and_Put_out));
  assign bit_extender_1_out = {{8{1'b0}}, adder_1_out};  // Bit_Extender bit_extender_1
  ROM #(.dataWidth(16)) rom_1 (.addr(PC_q), .data(rom_1_data), .sel(1'b1));
  Hex_Digit_Display hex_digit_display_4 (.value(register_1_q[3:0]));  // open: dp
  Multiplexer #(.width(16), .enable("false")) multiplexer_1 (
    .in0(multiplexer_11_out), .in1(bit_extender_1_out), .out(multiplexer_1_out),
    .sel(jump_control_1_output[2]));
  Jump_Control jump_control_1 (
    .A(rom_1_data[15]), .B(rom_1_data[14]), .C(rom_1_data[13]), .D(rom_1_data[12]), .Subop(rom_1_data[0]),
    .Output(jump_control_1_output));
  Branch_Control branch_control_1 (
    .A(rom_1_data[15]), .B(rom_1_data[14]), .C(rom_1_data[13]), .D(rom_1_data[12]), .Subop(rom_1_data[0]),
    .BN(branch_control_1_bn), .BP(branch_control_1_bp), .BX(branch_control_1_bx), .BZ(branch_control_1_bz));
  Multiplexer #(.width(8), .enable("false")) multiplexer_2 (
    .in0(multiplexer_9_out), .in1(multiplexer_4_out), .out(multiplexer_2_out), .sel(or_1_p2));
  Control control_1 (
    .A(rom_1_data[15]), .B(rom_1_data[14]), .C(rom_1_data[13]), .D(rom_1_data[12]), .Subop(rom_1_data[0]),
    .Halt(not_1_p1), .shift(control_1_shift), .ALUSrc(control_1_alusrc), .MemToReg(control_1_memtoreg),
    .RegWrite(control_1_regwrite), .MemRead(control_1_memread), .MemWrite(control_1_memwrite),
    .Branch(control_1_branch), .ALUOp1(control_1_aluop0[1]), .ALUOp0(control_1_aluop0[0]),
    .Put(control_1_put), .addi(control_1_addi));  // open: RegDst
  // OR_Gate or_1: pin names not known; wires that end beside it: jump_control_1_output[0], or_1_p2, jump_control_1_output[1], jump_control_1_output[2]
  Multiplexer #(.width(4), .enable("false")) multiplexer_3 (
    .in0(rom_1_data[4:1]), .in1(registers_1_read_data_2[3:0]), .out(multiplexer_3_out), .sel(rom_1_data[0]));
  Registers registers_1 (
    .Write_Enabled(control_1_regwrite), .Read_Register_1(rom_1_data[11:9]),
    .Read_Register_2(rom_1_data[8:6]), .Write_Register(rom_1_data[11:9]), .Write_Data(multiplexer_1_out),
    .Read_Data_1(rs), .Read_Data_2(registers_1_read_data_2), .Clock(CLOCK_out),
    .Clear(Clear_PC__Registers__and_Put_out));
  Multiplexer #(.select(3), .width(8), .enable("false")) multiplexer_4 (
    .in1(rom_1_data[8:1]), .in2(rs[7:0]), .in4(rom_1_data[8:1]), .out(multiplexer_4_out),
    .sel(jump_control_1_output));  // open: in0, in3, in5, in6, in7
  assign bit_extender_2_out = {{8{1'b0}}, rom_1_data[8:1]};  // Bit_Extender bit_extender_2
  assign bit_extender_3_out = {{8{rom_1_data[8]}}, rom_1_data[8:1]};  // Bit_Extender bit_extender_3
  Multiplexer #(.width(16), .enable("false")) multiplexer_5 (
    .in0(bit_extender_2_out), .in1(bit_extender_3_out), .out(multiplexer_5_out), .sel(control_1_addi));
  Multiplexer #(.width(16), .enable("false")) multiplexer_6 (
    .in0(registers_1_read_data_2), .in1(multiplexer_5_out), .out(rt_or_Imm), .sel(control_1_alusrc));
  Shifter #(.width(16)) shifter_1 (.in(rs), .\dist (multiplexer_3_out), .out(shifter_1_out));
  Shifter #(.width(16), .shift("lr")) shifter_2 (.in(rs), .\dist (multiplexer_3_out), .out(shifter_2_out));
  // NOT_Gate not_2: pin names not known; wires that end beside it: rs[15], not_2_p2, control_1_branch, not_2_p2, branch_control_1_bp
  // NOT_Gate not_3: pin names not known; wires that end beside it: not_3_p1, not_3_p2, not_3_p2, not_3_p2, control_1_branch, branch_control_1_bx
  // OR_Gate or_2: pin names not known; wires that end beside it: control_1_memwrite, or_2_p2, control_1_memread
  // NOT_Gate not_4: pin names not known; wires that end beside it: or_2_p2, not_4_p2
  _16_bit_ALU u_16_bit_alu_1 (
    .a(rs), .b(rt_or_Imm), .Operation(control_1_aluop0), .Zero(not_3_p1), .Result(n16_bit_alu_1_result));
  Multiplexer #(.width(16), .enable("false")) multiplexer_7 (
    .in0(shifter_1_out), .in1(shifter_2_out), .out(multiplexer_7_out), .sel(rom_1_data[12]));
  // AND_Gate BN: pin names not known; wires that end beside it: control_1_branch, rs[15], branch_control_1_bn, BN_p4
  // AND_Gate BP: pin names not known; wires that end beside it: BP_p1
  // AND_Gate BX: pin names not known; wires that end beside it: BX_p1
  // AND_Gate BZ: pin names not known; wires that end beside it: control_1_branch, branch_control_1_bz, not_3_p1, BZ_p4
  Multiplexer #(.width(16), .enable("false")) multiplexer_8 (
    .in0(registers_1_read_data_2), .in1(n16_bit_alu_1_result), .out(multiplexer_8_out), .sel(not_4_p2));
  Multiplexer #(.width(8), .enable("false")) multiplexer_9 (
    .in0(adder_1_out), .in1(rom_1_data[8:1]), .out(multiplexer_9_out), .sel(or_3_p5));
  // OR_Gate or_3: pin names not known; wires that end beside it: BN_p4, BP_p1, BX_p1, BZ_p4, or_3_p5
  RAM #(.dataWidth(16), .bus("separate")) ram_1 (
    .addr(multiplexer_8_out[7:0]), .din(rs), .data(ram_1_data), .str(control_1_memwrite), .sel(1'b1),
    .clk(CLOCK_out), .ld(control_1_memread), .clr(Clear_RAM_out));
  Multiplexer #(.width(16), .enable("false")) multiplexer_10 (
    .in0(multiplexer_8_out), .in1(ram_1_data), .out(multiplexer_10_out), .sel(control_1_memtoreg));
  Multiplexer #(.width(16), .enable("false")) multiplexer_11 (
    .in0(multiplexer_10_out), .in1(multiplexer_7_out), .out(multiplexer_11_out), .sel(control_1_shift));

  // Notes on the sheet:
  //   Zach Sadler
  //   zps6@pitt.edu
  //   Zach Sadler
  //   zps6@pitt.edu
  //   Zach Sadler
  //   zps6@pitt.edu
  //   Instruction Memory
  //   contents of rom_1 (hex, n*v repeats v):
  //   1fc1 ffe 1901 9fe c800 1001 12 ec19 1901 954 c800 2001 fff 7dc1 c000 9025 1ff ec19 7dc0 e03 ec00
  //   Zach Sadler
  //   zps6@pitt.edu
  //   RAM
  //   Zach Sadler
  //   zps6@pitt.edu
endmodule

module Registers (
  input  Write_Enabled,
  input  [2:0] Read_Register_1,
  input  [2:0] Read_Register_2,
  input  [2:0] Write_Register,
  input  [15:0] Write_Data,
  input  Clock,
  input  Clear,
  output [15:0] Read_Data_1,
  output [15:0] Read_Data_2
);

  wire and_1_p3, and_2_p3, and_3_p3, and_4_p3, and_5_p3, and_6_p3, and_7_p3, and_8_p3, decoder_1_out0,
       decoder_1_out1, decoder_1_out2, decoder_1_out3, decoder_1_out4, decoder_1_out5, decoder_1_out6,
       decoder_1_out7;
  wire [15:0] _000_q, _001_q, _010_q, _011_q, _100_q, _101_q, _110_q, _111_q;

  Decoder #(.select(3), .enable("false")) decoder_1 (
    .out0(decoder_1_out0), .out1(decoder_1_out1), .out2(decoder_1_out2), .out3(decoder_1_out3),
    .out4(decoder_1_out4), .out5(decoder_1_out5), .out6(decoder_1_out6), .out7(decoder_1_out7),
    .sel(Write_Register));
  // AND_Gate and_1: pin names not known; wires that end beside it: Write_Enabled, decoder_1_out7, and_1_p3
  // AND_Gate and_2: pin names not known; wires that end beside it: Write_Enabled, decoder_1_out6, and_2_p3
  // AND_Gate and_3: pin names not known; wires that end beside it: Write_Enabled, decoder_1_out5, and_3_p3
  // AND_Gate and_4: pin names not known; wires that end beside it: Write_Enabled, decoder_1_out4, and_4_p3
  // AND_Gate and_5: pin names not known; wires that end beside it: Write_Enabled, decoder_1_out3, and_5_p3
  // AND_Gate and_6: pin names not known; wires that end beside it: Write_Enabled, decoder_1_out2, and_6_p3
  // AND_Gate and_7: pin names not known; wires that end beside it: Write_Enabled, decoder_1_out1, and_7_p3
  // AND_Gate and_8: pin names not known; wires that end beside it: Write_Enabled, decoder_1_out0, and_8_p3
  Register #(.width(16)) _111 (.D(Write_Data), .en(and_1_p3), .Q(_111_q), .clk(Clock), .clr(Clear));
  Register #(.width(16)) _110 (.D(Write_Data), .en(and_2_p3), .Q(_110_q), .clk(Clock), .clr(Clear));
  Register #(.width(16)) _101 (.D(Write_Data), .en(and_3_p3), .Q(_101_q), .clk(Clock), .clr(Clear));
  Register #(.width(16)) _100 (.D(Write_Data), .en(and_4_p3), .Q(_100_q), .clk(Clock), .clr(Clear));
  Register #(.width(16)) _011 (.D(Write_Data), .en(and_5_p3), .Q(_011_q), .clk(Clock), .clr(Clear));
  Register #(.width(16)) _010 (.D(Write_Data), .en(and_6_p3), .Q(_010_q), .clk(Clock), .clr(Clear));
  Register #(.width(16)) _001 (.D(Write_Data), .en(and_7_p3), .Q(_001_q), .clk(Clock), .clr(Clear));
  Register #(.width(16)) _000 (.D(Write_Data), .en(and_8_p3), .Q(_000_q), .clk(Clock), .clr(Clear));
  Multiplexer #(.select(3), .width(16), .disabled(0), .enable("false")) multiplexer_1 (
    .in0(_000_q), .in1(_001_q), .in2(_010_q), .in3(_011_q), .in4(_100_q), .in5(_101_q), .in6(_110_q),
    .in7(_111_q), .out(Read_Data_1), .sel(Read_Register_1));
  Multiplexer #(.select(3), .width(16), .enable("false")) multiplexer_2 (
    .in0(_000_q), .in1(_001_q), .in2(_010_q), .in3(_011_q), .in4(_100_q), .in5(_101_q), .in6(_110_q),
    .in7(_111_q), .out(Read_Data_2), .sel(Read_Register_2));

  // Notes on the sheet:
  //   This is Lab11 extended to 8 registers
endmodule

module _16_bit_ALU (
  input  [1:0] Operation,
  input  [15:0] a,
  input  [15:0] b,
  output Zero,
  output [15:0] Result
);

  wire not_1_p1, subtractor_1_bout;
  wire [15:0] adder_1_out, adder_2_out, AND_p3, multiplexer_1_out, NOR_p3, subtractor_1_out;

  Adder #(.width(16)) adder_1 (.a(a), .b(b), .out(adder_1_out));  // open: cin, cout
  Subtractor #(.width(16)) subtractor_1 (.a(a), .b(b), .out(subtractor_1_out), .bin(1'b1), .bout(subtractor_1_bout));
  // AND_Gate AND: pin names not known; wires that end beside it: a, b, AND_p3
  // NOR_Gate NOR: pin names not known; wires that end beside it: a, b, NOR_p3
  Adder #(.width(16)) adder_2 (.a(subtractor_1_out), .b(16'h1), .out(adder_2_out));  // open: cin, cout
  Multiplexer #(.width(16), .enable("false")) multiplexer_1 (
    .in0(subtractor_1_out), .in1(adder_2_out), .out(multiplexer_1_out), .sel(subtractor_1_bout));
  Multiplexer #(.select(2), .width(16), .enable("false")) multiplexer_2 (
    .in0(AND_p3), .in1(NOR_p3), .in2(adder_1_out), .in3(multiplexer_1_out), .out(Result), .sel(Operation));
  // NOT_Gate not_1: pin names not known; wires that end beside it: not_1_p1, Zero
  // OR_Gate or_1: pin names not known; wires that end beside it: a[0], a[1], a[2], a[3], a[4], a[5], a[6], a[7], a[8], a[9], a[10], a[11], a[12], a[13], a[14], a[15], not_1_p1

  // Notes on the sheet:
  //   00 is AND, 01 is NOR, 10 is ADD, 11 is SUB
endmodule

module Control (
  input  A,
  input  B,
  input  C,
  input  D,
  input  Subop,
  output RegDst,
  output ALUSrc,
  output MemToReg,
  output RegWrite,
  output MemRead,
  output MemWrite,
  output Branch,
  output ALUOp1,
  output ALUOp0,
  output Halt,
  output Put,
  output addi,
  output shift
);

  wire and_1_p1, and_2_p1, and_4_p3, and_5_p2, and_6_p2, and_7_p5, and_8_p4, and_9_p4, and_11_p3, and_12_p3,
       and_13_p2, and_14_p2, and_16_p4, and_17_p5, and_20_p4, and_21_p3, and_22_p4, and_23_p4, and_24_p4,
       and_25_p2, and_29_p4, not_1_p2, not_2_p2, not_3_p2, not_4_p2, not_5_p2, not_6_p2, not_7_p2, not_8_p2,
       not_9_p2, not_10_p2, not_11_p2, not_12_p2, not_13_p2, not_14_p2, not_15_p2, not_16_p2, not_17_p2,
       not_18_p2, not_19_p2, not_20_p2, not_21_p2, not_22_p2, not_25_p2, not_26_p2, not_27_p2, not_28_p2,
       not_29_p2, not_30_p2, not_31_p2, not_32_p2, not_33_p2, not_34_p2, not_35_p2, not_36_p2, not_37_p2,
       not_38_p2, not_39_p2, not_40_p2, not_41_p2, not_42_p2, not_43_p2, not_44_p2, not_45_p2, not_46_p2,
       not_47_p2, not_48_p2, not_49_p2, not_50_p2, not_51_p2, not_52_p2, not_53_p1, not_54_p1, not_54_p2,
       not_54_p3, not_54_p4, not_56_p2, or_1_p2, or_3_p3, or_4_p5;

  // NOT_Gate not_1: pin names not known; wires that end beside it: A, not_1_p2
  // NOT_Gate not_2: pin names not known; wires that end beside it: B, not_2_p2
  // NOT_Gate not_3: pin names not known; wires that end beside it: A, not_3_p2, not_3_p2
  // NOT_Gate not_4: pin names not known; wires that end beside it: C, not_4_p2
  // NOT_Gate not_5: pin names not known; wires that end beside it: D, not_5_p2, not_5_p2
  // NOT_Gate not_6: pin names not known; wires that end beside it: A, not_6_p2
  // NOT_Gate not_7: pin names not known; wires that end beside it: B, not_7_p2
  // NOT_Gate not_8: pin names not known; wires that end beside it: C, not_8_p2
  // NOT_Gate not_9: pin names not known; wires that end beside it: D, not_9_p2
  // NOT_Gate not_10: pin names not known; wires that end beside it: A, not_10_p2, not_10_p2
  // NOT_Gate not_11: pin names not known; wires that end beside it: Subop, not_11_p2, not_11_p2
  // NOT_Gate not_12: pin names not known; wires that end beside it: A, not_12_p2
  // NOT_Gate not_13: pin names not known; wires that end beside it: C, not_13_p2
  // NOT_Gate not_14: pin names not known; wires that end beside it: B, not_14_p2
  // NOT_Gate not_15: pin names not known; wires that end beside it: C, not_15_p2, not_15_p2
  // NOT_Gate not_16: pin names not known; wires that end beside it: Subop, not_16_p2, not_16_p2
  // NOT_Gate not_17: pin names not known; wires that end beside it: C, not_17_p2
  // NOT_Gate not_18: pin names not known; wires that end beside it: D, not_18_p2
  // NOT_Gate not_19: pin names not known; wires that end beside it: B, not_19_p2
  // NOT_Gate not_20: pin names not known; wires that end beside it: C, not_20_p2
  // NOT_Gate not_21: pin names not known; wires that end beside it: C, not_21_p2
  // AND_Gate and_1: pin names not known; wires that end beside it: and_1_p1
  // NOT_Gate not_22: pin names not known; wires that end beside it: D, not_22_p2, A, B, C, not_22_p2, Subop
  // AND_Gate and_2: pin names not known; wires that end beside it: and_2_p1
  // NOT_Gate not_23: pin names not known; wires that end beside it: D, A, B, C
  // NOT_Gate not_24: pin names not known; wires that end beside it: Subop
  // NOT_Gate not_25: pin names not known; wires that end beside it: Subop, not_25_p2
  // AND_Gate and_3: pin names not known; wires that end beside it: B, C, Subop, MemWrite
  // NOT_Gate not_26: pin names not known; wires that end beside it: B, not_26_p2, not_26_p2
  // NOT_Gate not_27: pin names not known; wires that end beside it: A, not_27_p2
  // NOT_Gate not_28: pin names not known; wires that end beside it: C, not_28_p2
  // NOT_Gate not_29: pin names not known; wires that end beside it: C, not_29_p2
  // NOT_Gate not_30: pin names not known; wires that end beside it: A, not_30_p2, not_30_p2
  // NOT_Gate not_31: pin names not known; wires that end beside it: C, not_31_p2
  // NOT_Gate not_32: pin names not known; wires that end beside it: D, not_32_p2
  // NOT_Gate not_33: pin names not known; wires that end beside it: C, not_33_p2
  // NOT_Gate not_34: pin names not known; wires that end beside it: D, not_34_p2
  // NOT_Gate not_35: pin names not known; wires that end beside it: A, not_35_p2, not_35_p2
  // NOT_Gate not_36: pin names not known; wires that end beside it: B, not_36_p2, not_36_p2
  // NOT_Gate not_37: pin names not known; wires that end beside it: B, not_37_p2
  // NOT_Gate not_38: pin names not known; wires that end beside it: B, not_38_p2, not_38_p2
  // NOT_Gate not_39: pin names not known; wires that end beside it: A, not_39_p2
  // NOT_Gate not_40: pin names not known; wires that end beside it: B, not_40_p2, not_39_p2
  // NOT_Gate not_41: pin names not known; wires that end beside it: D, not_41_p2
  // NOT_Gate not_42: pin names not known; wires that end beside it: C, not_42_p2
  // NOT_Gate not_43: pin names not known; wires that end beside it: D, not_43_p2
  // NOT_Gate not_44: pin names not known; wires that end beside it: A, not_44_p2, not_44_p2
  // NOT_Gate not_45: pin names not known; wires that end beside it: B, not_45_p2
  // NOT_Gate not_46: pin names not known; wires that end beside it: C, not_46_p2
  // NOT_Gate not_47: pin names not known; wires that end beside it: D, not_47_p2
  // NOT_Gate not_48: pin names not known; wires that end beside it: A, not_48_p2
  // NOT_Gate not_49: pin names not known; wires that end beside it: C, not_49_p2
  // NOT_Gate not_50: pin names not known; wires that end beside it: D, not_50_p2, not_50_p2
  // NOT_Gate not_51: pin names not known; wires that end beside it: A, not_51_p2
  // NOT_Gate not_52: pin names not known; wires that end beside it: C, not_52_p2
  // AND_Gate and_4: pin names not known; wires that end beside it: not_1_p2, not_2_p2, and_4_p3
  // AND_Gate and_5: pin names not known; wires that end beside it: not_4_p2, and_5_p2
  // AND_Gate and_6: pin names not known; wires that end beside it: B, and_6_p2
  // AND_Gate and_7: pin names not known; wires that end beside it: not_6_p2, not_7_p2, not_8_p2, not_9_p2, and_7_p5
  // AND_Gate and_8: pin names not known; wires that end beside it: B, C, D, and_8_p4
  // AND_Gate and_9: pin names not known; wires that end beside it: B, C, D, and_9_p4, and_9_p4
  // NOT_Gate not_53: pin names not known; wires that end beside it: not_53_p1
  // AND_Gate and_10: pin names not known; wires that end beside it: B, C, D, MemToReg
  // AND_Gate and_11: pin names not known; wires that end beside it: not_12_p2, not_13_p2, and_11_p3
  // AND_Gate and_12: pin names not known; wires that end beside it: not_14_p2, C, and_12_p3, and_11_p3
  // AND_Gate and_13: pin names not known; wires that end beside it: B, and_13_p2
  // AND_Gate and_14: pin names not known; wires that end beside it: B, and_14_p2
  // NOT_Gate not_54: pin names not known; wires that end beside it: not_54_p1, not_54_p2, not_54_p3, not_54_p4
  // AND_Gate and_15: pin names not known; wires that end beside it: A, B, not_17_p2, not_18_p2, not_54_p1
  // AND_Gate and_16: pin names not known; wires that end beside it: A, not_19_p2, not_20_p2, and_16_p4, and_16_p4
  // NOT_Gate not_55: pin names not known; wires that end beside it: not_54_p3
  // AND_Gate and_17: pin names not known; wires that end beside it: A, not_21_p2, B, D, and_17_p5
  // NOT_Gate not_56: pin names not known; wires that end beside it: and_2_p1, not_56_p2
  // AND_Gate and_18: pin names not known; wires that end beside it: B, C, D, not_25_p2, MemRead
  // AND_Gate and_19: pin names not known; wires that end beside it: A, Branch
  // AND_Gate and_20: pin names not known; wires that end beside it: not_27_p2, not_28_p2, not_29_p2, and_20_p4
  // AND_Gate and_21: pin names not known; wires that end beside it: not_31_p2, not_32_p2, and_21_p3
  // AND_Gate and_22: pin names not known; wires that end beside it: B, not_33_p2, not_34_p2, and_22_p4
  // AND_Gate and_23: pin names not known; wires that end beside it: C, D, Subop, and_23_p4
  // AND_Gate and_24: pin names not known; wires that end beside it: not_37_p2, D, Subop, and_24_p4
  // AND_Gate and_25: pin names not known; wires that end beside it: A, and_25_p2
  // AND_Gate and_26: pin names not known; wires that end beside it: not_40_p2, C, not_41_p2, Subop, Halt
  // AND_Gate and_27: pin names not known; wires that end beside it: A, B, not_42_p2, not_43_p2, Put
  // AND_Gate and_28: pin names not known; wires that end beside it: not_45_p2, not_46_p2, not_47_p2, Subop, addi
  // AND_Gate and_29: pin names not known; wires that end beside it: not_48_p2, B, not_49_p2, and_29_p4
  // OR_Gate or_1: pin names not known; wires that end beside it: and_29_p4, or_1_p2, shift
  // AND_Gate and_30: pin names not known; wires that end beside it: not_51_p2, B, not_52_p2, D, or_1_p2
  // OR_Gate or_2: pin names not known; wires that end beside it: and_4_p3, and_5_p2, and_6_p2, RegDst
  // OR_Gate or_3: pin names not known; wires that end beside it: and_7_p5, and_8_p4, or_3_p3
  // AND_Gate and_31: pin names not known; wires that end beside it: or_3_p3, not_53_p1, ALUSrc
  // OR_Gate or_4: pin names not known; wires that end beside it: and_12_p3, and_1_p1, and_13_p2, and_14_p2, or_4_p5
  // AND_Gate and_32: pin names not known; wires that end beside it: or_4_p5, not_54_p2, not_56_p2, RegWrite
  // NOT_Gate not_57: pin names not known; wires that end beside it: and_17_p5, not_54_p4
  // OR_Gate or_5: pin names not known; wires that end beside it: and_20_p4, and_21_p3, and_22_p4, ALUOp1
  // OR_Gate or_6: pin names not known; wires that end beside it: and_23_p4, and_24_p4, and_25_p2, ALUOp0

  // Notes on the sheet:
  //   Note this is not actually used
endmodule

module Branch_Control (
  input  A,
  input  B,
  input  C,
  input  D,
  input  Subop,
  output BN,
  output BP,
  output BX,
  output BZ
);

  wire and_1_p1, and_2_p1, not_1_p2, not_2_p2, not_3_p2, not_4_p2, not_5_p2, not_6_p2, not_7_p2;

  // NOT_Gate not_1: pin names not known; wires that end beside it: B, not_1_p2, A, not_1_p2
  // AND_Gate and_1: pin names not known; wires that end beside it: and_1_p1
  // NOT_Gate not_2: pin names not known; wires that end beside it: C, not_2_p2, not_2_p2
  // NOT_Gate not_3: pin names not known; wires that end beside it: D, not_3_p2, not_3_p2
  // NOT_Gate not_4: pin names not known; wires that end beside it: Subop, not_4_p2
  // NOT_Gate not_5: pin names not known; wires that end beside it: B, not_5_p2, A, not_5_p2
  // AND_Gate and_2: pin names not known; wires that end beside it: and_2_p1
  // NOT_Gate not_6: pin names not known; wires that end beside it: C, not_6_p2, not_6_p2, D
  // NOT_Gate not_7: pin names not known; wires that end beside it: Subop, not_7_p2
  // AND_Gate and_3: pin names not known; wires that end beside it: and_1_p1, not_4_p2, BN
  // AND_Gate and_4: pin names not known; wires that end beside it: and_1_p1, Subop, BP
  // AND_Gate and_5: pin names not known; wires that end beside it: and_2_p1, not_7_p2, BX
  // AND_Gate and_6: pin names not known; wires that end beside it: and_2_p1, Subop, BZ
endmodule

module Jump_Control (
  input  A,
  input  B,
  input  C,
  input  D,
  input  Subop,
  output [2:0] Output
);

  wire and_2_p3, not_1_p2, not_2_p2, not_3_p2;

  // AND_Gate and_1: pin names not known; wires that end beside it: Output[0]
  // NOT_Gate not_1: pin names not known; wires that end beside it: C, not_1_p2, A, B, not_1_p2, D
  // AND_Gate and_2: pin names not known; wires that end beside it: A, B, and_2_p3
  // NOT_Gate not_2: pin names not known; wires that end beside it: D, not_2_p2, C, not_2_p2
  // NOT_Gate not_3: pin names not known; wires that end beside it: Subop, not_3_p2
  // AND_Gate and_3: pin names not known; wires that end beside it: and_2_p3, not_3_p2, Output[1]
  // AND_Gate and_4: pin names not known; wires that end beside it: and_2_p3, Subop, Output[2]
endmodule
